// Logisim project alu.circ as structural Verilog: 1 circuit, main circuit alu
module alu (
  input  [31:0] A,
  input  [31:0] B,
  input  [3:0] ALUSel,
  output [31:0] Result
);

  wire comparator_1_lt;
  wire [4:0] bitselector_1_out, bitselector_2_out, bitselector_3_out;
  wire [31:0] add0, and7, mul8, mulh9, mulhu11, or6, sll1, slt2, sra13, srl5, sub12, xor4;
  wire [63:0] bit_extender_2_out, bit_extender_3_out, bit_extender_4_out, bit_extender_5_out,
       multiplier_1_out, multiplier_2_out;

  Multiplexer #(.enable("false"), .select(4), .width(32)) multiplexer_1 (
    .in0(add0), .in1(sll1), .in2(slt2), .in4(xor4), .in5(srl5), .in6(or6), .in7(and7), .in8(mul8),
    .in9(mulh9), .in11(mulhu11), .in12(sub12), .in13(sra13), .in15(B), .out(Result), .sel(ALUSel));  // open: in3, in10, in14
  BitSelector #(.group(5), .width(32)) bitselector_1 (.in(B), .out(bitselector_1_out), .sel(3'b000));
  Adder #(.width(32)) adder_1 (.a(A), .b(B), .out(add0));  // open: cin, cout
  Shifter #(.width(32)) shifter_1 (.in(A), .\dist (bitselector_1_out), .out(sll1));
  Comparator #(.width(32)) comparator_1 (.a(A), .b(B), .lt(comparator_1_lt));  // open: gt, eq
  assign slt2 = {{31{1'b0}}, comparator_1_lt};  // Bit_Extender bit_extender_1
  assign bit_extender_2_out = {{32{A[31]}}, A};  // Bit_Extender bit_extender_2
  assign bit_extender_3_out = {{32{B[31]}}, B};  // Bit_Extender bit_extender_3
  assign bit_extender_4_out = {{32{1'b0}}, A};  // Bit_Extender bit_extender_4
  assign bit_extender_5_out = {{32{1'b0}}, B};  // Bit_Extender bit_extender_5
  BitSelector #(.group(5), .width(32)) bitselector_2 (.in(B), .out(bitselector_2_out), .sel(3'b000));
  Multiplier #(.mode("twosComplement"), .width(64)) multiplier_1 (
    .a(bit_extender_2_out), .b(bit_extender_3_out), .out(multiplier_1_out));  // open: cin, cout
  Multiplier #(.width(64)) multiplier_2 (
    .a(bit_extender_4_out), .b(bit_extender_5_out), .out(multiplier_2_out));  // open: cin, cout
  BitSelector #(.group(5), .width(32)) bitselector_3 (.in(B), .out(bitselector_3_out), .sel(3'b000));
  assign xor4 = A ^ B;  // XOR_Gate xor_1, 32 bits wide
  Shifter #(.shift("lr"), .width(32)) shifter_2 (.in(A), .\dist (bitselector_2_out), .out(srl5));
  assign or6 = A | B;  // OR_Gate or_1, 32 bits wide
  assign and7 = A & B;  // AND_Gate and_1, 32 bits wide
  Multiplier #(.mode("twosComplement"), .width(32)) multiplier_3 (.a(A), .b(B), .out(mul8));  // open: cin, cout
  BitSelector #(.group(32), .width(64)) bitselector_4 (.in(multiplier_1_out), .out(mulh9), .sel(1'b1));
  BitSelector #(.group(32), .width(64)) bitselector_5 (.in(multiplier_2_out), .out(mulhu11), .sel(1'b1));
  Subtractor #(.width(32)) subtractor_1 (.a(A), .b(B), .out(sub12));  // open: bin, bout
  Shifter #(.shift("ar"), .width(32)) shifter_3 (.in(A), .\dist (bitselector_3_out), .out(sra13));

  // Other names for the same wires on the sheet: bsel15[31:0] = B

  // Notes on the sheet:
  //   INPUTS to your circuit
  //   DON'T CHANGE THE LOCATIONS OF THE INPUTS AND OUTPUTS!
  //   OUTPUT from your circuit
endmodule
