// Logisim project cpu.circ as structural Verilog: 1 circuit, main circuit cpu
module cpu (
  input  clk,
  input  [31:0] INSTRUCTION,
  input  [31:0] READ_DATA,
  output [31:0] WRITE_ADDRESS,
  output [31:0] PROGRAM_COUNTER,
  output [31:0] ra,
  output [31:0] sp,
  output [31:0] t0,
  output [31:0] t1,
  output [31:0] t2,
  output [31:0] s0,
  output [31:0] s1,
  output [31:0] a0,
  output [31:0] tohost,
  output [3:0] WRITE_ENABLE,
  output [31:0] WRITE_DATA
);

  wire ASel, BrEq, BrLt, BrUn, BSel, CSRSel, CSRWen, MemRW, PCSel, register_2_q, RegWEn;
  wire [1:0] bitselector_7_out, bitselector_8_out, Reminder, WBSel;
  wire [2:0] funct3, ImmSel;
  wire [3:0] ALUSel, multiplexer_8_out, shifter_6_out;
  wire [4:0] bit_extender_2_out, bit_extender_3_out, bitselector_1_out, bitselector_2_out, bitselector_3_out,
       shifter_4_out, shifter_7_out;
  wire [7:0] bitselector_9_out;
  wire [11:0] bitselector_4_out;
  wire [15:0] bitselector_10_out;
  wire [31:0] bit_extender_1_out, CSRSrc, Imm, INSTRUCTION1, multiplexer_1_out, multiplexer_5_out,
       multiplexer_6_out, NEXT_PC, PROCESSED_READ_DATA, rd, READ_BYTE, READ_HALF, READ_WORD, register_1_q,
       register_3_q, register_4_q, rs1, rs2, shifter_1_out, shifter_2_out, shifter_3_out;

  Adder #(.width(32)) adder_1 (.a(PROGRAM_COUNTER), .b(32'h4), .out(NEXT_PC));  // open: cin, cout
  Multiplexer #(.enable("false"), .width(32)) multiplexer_1 (
    .in0(NEXT_PC), .in1(WRITE_ADDRESS), .out(multiplexer_1_out), .sel(PCSel));
  Register #(.width(32)) PC (.D(multiplexer_1_out), .en(1'b1), .clk(clk), .Q(PROGRAM_COUNTER));  // open: clr
  BitSelector #(.group(5), .width(32)) bitselector_1 (.in(shifter_1_out), .out(bitselector_1_out), .sel(3'b000));
  Shifter #(.shift("lr"), .width(32)) shifter_1 (.in(INSTRUCTION1), .\dist (5'b01111), .out(shifter_1_out));
  BitSelector #(.group(5), .width(32)) bitselector_2 (.in(shifter_1_out), .out(bitselector_2_out), .sel(3'b001));
  BitSelector #(.group(5), .width(32)) bitselector_3 (.in(shifter_2_out), .out(bitselector_3_out), .sel(3'b000));
  Shifter #(.shift("lr"), .width(32)) shifter_2 (.in(INSTRUCTION1), .\dist (5'b00111), .out(shifter_2_out));
  Register #(.width(32)) register_1 (.D(INSTRUCTION), .en(1'b1), .clk(clk), .Q(register_1_q));  // open: clr
  assign bit_extender_1_out = {{27{1'b0}}, bitselector_1_out};  // Bit_Extender bit_extender_1
  imm_gen imm_gen_1 (.inst(INSTRUCTION1), .ImmSel(ImmSel), .imm(Imm));
  BitSelector #(.group(12), .width(32)) bitselector_4 (.in(Imm), .out(bitselector_4_out), .sel(2'b00));
  Register #(.width(1)) register_2 (.D(PCSel), .en(1'b1), .clk(clk), .Q(register_2_q));  // open: clr
  Multiplexer #(.enable("false"), .width(32)) multiplexer_2 (
    .in0(rs1), .in1(bit_extender_1_out), .out(CSRSrc), .sel(CSRSel));
  Multiplexer #(.enable("false"), .width(32)) multiplexer_3 (
    .in0(register_1_q), .in1(32'h13), .out(INSTRUCTION1), .sel(register_2_q));
  regfile regfile_1 (
    .rs1(bitselector_1_out), .rs2(bitselector_2_out), .rd(bitselector_3_out), .Write_Data(rd),
    .RegWEn(RegWEn), .clk(clk), .ra(ra), .sp(sp), .t0(t0), .t1(t1), .t2(t2), .s0(s0), .s1(s1), .a0(a0),
    .Read_Data_1(rs1), .Read_Data_2(rs2));
  // csr csr_1: pin names not known; wires that end beside it: bitselector_4_out, CSRSrc, CSRWen, clk, tohost
  Register #(.width(32)) register_3 (.D(NEXT_PC), .en(1'b1), .clk(clk), .Q(register_3_q));  // open: clr
  control_logic control_logic_1 (
    .CSRWen(CSRWen), .PCSel(PCSel), .RegWEn(RegWEn), .ImmSel(ImmSel), .BrUn(BrUn), .ASel(ASel), .BSel(BSel),
    .ALUSel(ALUSel), .MemRW(MemRW), .WBSel(WBSel), .CSRSel(CSRSel), .inst(INSTRUCTION1), .BrEq(BrEq),
    .BrLt(BrLt));
  Multiplexer #(.enable("false"), .select(2), .width(32)) multiplexer_4 (
    .in0(PROCESSED_READ_DATA), .in1(WRITE_ADDRESS), .in2(register_3_q), .out(rd), .sel(WBSel));  // open: in3
  branch_comp branch_comp_1 (.rs1(rs1), .rs2(rs2), .BrUn(BrUn), .BrEq(BrEq), .BrLt(BrLt));
  Register #(.width(32)) register_4 (.D(PROGRAM_COUNTER), .en(1'b1), .clk(clk), .Q(register_4_q));  // open: clr
  Multiplexer #(.enable("false"), .width(32)) multiplexer_5 (
    .in0(rs1), .in1(register_4_q), .out(multiplexer_5_out), .sel(ASel));
  Multiplexer #(.enable("false"), .width(32)) multiplexer_6 (.in0(rs2), .in1(Imm), .out(multiplexer_6_out), .sel(BSel));
  Shifter #(.shift("lr"), .width(32)) shifter_3 (.in(INSTRUCTION1), .\dist (5'b01100), .out(shifter_3_out));
  BitSelector #(.group(3), .width(32)) bitselector_5 (.in(shifter_3_out), .out(funct3), .sel(4'b0000));
  BitSelector #(.group(2), .width(32)) bitselector_6 (.in(WRITE_ADDRESS), .out(Reminder), .sel(4'b0000));
  alu alu_1 (.Result(WRITE_ADDRESS), .A(multiplexer_5_out), .B(multiplexer_6_out), .ALUSel(ALUSel));
  assign bit_extender_2_out = {{3{1'b0}}, Reminder};  // Bit_Extender bit_extender_2
  Shifter #(.width(5)) shifter_4 (.in(bit_extender_2_out), .\dist (3'b011), .out(shifter_4_out));
  Multiplexer #(.enable("false"), .select(2), .width(32)) multiplexer_7 (
    .in0(READ_BYTE), .in1(READ_HALF), .in2(READ_WORD), .out(PROCESSED_READ_DATA), .sel(bitselector_7_out));  // open: in3
  BitSelector #(.group(2), .width(3)) bitselector_7 (.in(funct3), .out(bitselector_7_out), .sel(1'b0));
  Multiplexer #(.enable("false"), .select(2), .width(4)) multiplexer_8 (
    .in0(4'b0001), .in1(4'b0011), .in2(4'b1111), .out(multiplexer_8_out), .sel(bitselector_8_out));  // open: in3
  BitSelector #(.group(2), .width(3)) bitselector_8 (.in(funct3), .out(bitselector_8_out), .sel(1'b0));
  Shifter #(.shift("lr"), .width(32)) shifter_5 (.in(READ_DATA), .\dist (shifter_4_out), .out(READ_WORD));
  Shifter #(.width(4)) shifter_6 (.in(multiplexer_8_out), .\dist (Reminder), .out(shifter_6_out));
  assign bit_extender_3_out = {{3{1'b0}}, Reminder};  // Bit_Extender bit_extender_3
  BitSelector #(.group(8), .width(32)) bitselector_9 (.in(READ_WORD), .out(bitselector_9_out), .sel(2'b00));
  BitSelector #(.group(16), .width(32)) bitselector_10 (.in(READ_WORD), .out(bitselector_10_out), .sel(1'b0));
  Multiplexer #(.enable("false"), .width(4)) multiplexer_9 (
    .in0(4'b0000), .in1(shifter_6_out), .out(WRITE_ENABLE), .sel(MemRW));
  Shifter #(.width(5)) shifter_7 (.in(bit_extender_3_out), .\dist (3'b011), .out(shifter_7_out));
  assign READ_BYTE = {{24{bitselector_9_out[7]}}, bitselector_9_out};  // Bit_Extender bit_extender_4
  assign READ_HALF = {{16{bitselector_10_out[15]}}, bitselector_10_out};  // Bit_Extender bit_extender_5
  Shifter #(.width(32)) shifter_8 (.in(rs2), .\dist (shifter_7_out), .out(WRITE_DATA));

  // Other names for the same wires on the sheet: ALUResult[31:0] = WRITE_ADDRESS

  // Notes on the sheet:
  //   Output to IMEM
  //   IMEM (do **NOT** move this)
  //   Inputs from IMEM
  //   It is OK to move the PC, RegFile, ALU, MEM, Branch Comp, Imm Gen, and Control Logic to wherever is most convenient for you when constructing your CPU, and to delete this text
  //   Inputs/Outputs for testing. Do **NOT** move these.
  //   Outputs To DMEM
  //   DMEM (do **NOT** move this)
  //   Inputs From DMEM
endmodule
