// Logisim project imm-gen.circ as structural Verilog: 1 circuit, main circuit imm_gen
module imm_gen (
  input  [31:0] inst,
  input  [2:0] ImmSel,
  output [31:0] imm
);

  wire comparator_1_eq, i_7, i_20, i_31;
  wire [3:0] bitselector_5_out, bitselector_6_out;
  wire [5:0] bitselector_4_out;
  wire [6:0] opcode;
  wire [7:0] bitselector_7_out;
  wire [10:0] bitselector_8_out;
  wire [31:0] adder_1_out, adder_2_out, adder_4_out, adder_5_out, adder_7_out, adder_8_out, adder_9_out,
       adder_10_out, adder_11_out, adder_14_out, bit_extender_1_out, bit_extender_2_out, bit_extender_3_out,
       bit_extender_4_out, bit_extender_5_out, bit_extender_6_out, bit_extender_7_out, bit_extender_8_out,
       bit_extender_9_out, bit_extender_10_out, bit_extender_11_out, bit_extender_12_out,
       bit_extender_13_out, bit_extender_14_out, i_11_8, i_19_12, i_24_21, i_30_20, i_30_25, imm_I, imm_S,
       imm_SB, imm_U, imm_UJ, multiplexer_2_out, shifter_1_out, shifter_2_out, shifter_3_out, shifter_4_out,
       shifter_5_out, shifter_6_out, shifter_12_out, shifter_13_out, shifter_14_out, shifter_15_out,
       shifter_16_out, shifter_17_out;

  BitSelector #(.width(32)) bitselector_1 (.in(inst), .out(i_31), .sel({5{1'b1}}));
  BitSelector #(.width(32)) bitselector_2 (.in(inst), .out(i_20), .sel(5'b10100));
  BitSelector #(.width(32)) bitselector_3 (.in(inst), .out(i_7), .sel(5'b00111));
  assign bit_extender_1_out = {{31{i_31}}, i_31};  // Bit_Extender bit_extender_1
  Shifter #(.width(32)) shifter_1 (.in(bit_extender_1_out), .\dist (5'b01011), .out(shifter_1_out));
  assign bit_extender_2_out = {{31{1'b0}}, i_20};  // Bit_Extender bit_extender_2
  BitSelector #(.group(6), .width(32)) bitselector_4 (.in(shifter_2_out), .out(bitselector_4_out), .sel(3'b000));
  Shifter #(.shift("lr"), .width(32)) shifter_2 (.in(inst), .\dist (5'b11001), .out(shifter_2_out));
  BitSelector #(.group(4), .width(32)) bitselector_5 (.in(shifter_3_out), .out(bitselector_5_out), .sel(3'b000));
  Shifter #(.shift("lr"), .width(32)) shifter_3 (.in(inst), .\dist (5'b10101), .out(shifter_3_out));
  BitSelector #(.group(4), .width(32)) bitselector_6 (.in(shifter_4_out), .out(bitselector_6_out), .sel(3'b000));
  Shifter #(.shift("lr"), .width(32)) shifter_4 (.in(inst), .\dist (5'b01000), .out(shifter_4_out));
  BitSelector #(.group(8), .width(32)) bitselector_7 (.in(shifter_5_out), .out(bitselector_7_out), .sel(2'b00));
  Shifter #(.shift("lr"), .width(32)) shifter_5 (.in(inst), .\dist (5'b01100), .out(shifter_5_out));
  BitSelector #(.group(11), .width(32)) bitselector_8 (.in(shifter_6_out), .out(bitselector_8_out), .sel(2'b00));
  Shifter #(.shift("lr"), .width(32)) shifter_6 (.in(inst), .\dist (5'b10100), .out(shifter_6_out));
  Adder #(.width(32)) adder_1 (.a(shifter_1_out), .b(i_30_25), .out(adder_1_out));  // open: cin, cout
  Adder #(.width(32)) adder_2 (.a(i_24_21), .b(bit_extender_2_out), .out(adder_2_out));  // open: cin, cout
  assign bit_extender_3_out = {{26{1'b0}}, bitselector_4_out};  // Bit_Extender bit_extender_3
  assign bit_extender_4_out = {{28{1'b0}}, bitselector_5_out};  // Bit_Extender bit_extender_4
  assign bit_extender_5_out = {{28{1'b0}}, bitselector_6_out};  // Bit_Extender bit_extender_5
  assign bit_extender_6_out = {{24{1'b0}}, bitselector_7_out};  // Bit_Extender bit_extender_6
  assign bit_extender_7_out = {{21{1'b0}}, bitselector_8_out};  // Bit_Extender bit_extender_7
  Adder #(.width(32)) adder_3 (.a(adder_1_out), .b(adder_2_out), .out(imm_I));  // open: cin, cout
  Shifter #(.width(32)) shifter_7 (.in(bit_extender_3_out), .\dist (5'b00101), .out(i_30_25));
  Shifter #(.width(32)) shifter_8 (.in(bit_extender_4_out), .\dist (5'b00001), .out(i_24_21));
  Shifter #(.width(32)) shifter_9 (.in(bit_extender_5_out), .\dist (5'b00001), .out(i_11_8));
  Shifter #(.width(32)) shifter_10 (.in(bit_extender_6_out), .\dist (5'b01100), .out(i_19_12));
  Shifter #(.width(32)) shifter_11 (.in(bit_extender_7_out), .\dist (5'b10100), .out(i_30_20));
  assign bit_extender_8_out = {{31{i_31}}, i_31};  // Bit_Extender bit_extender_8
  Shifter #(.width(32)) shifter_12 (.in(bit_extender_8_out), .\dist (5'b01011), .out(shifter_12_out));
  assign bit_extender_9_out = {{31{1'b0}}, i_7};  // Bit_Extender bit_extender_9
  Adder #(.width(32)) adder_4 (.a(shifter_12_out), .b(i_30_25), .out(adder_4_out));  // open: cin, cout
  Adder #(.width(32)) adder_5 (.a(i_11_8), .b(bit_extender_9_out), .out(adder_5_out));  // open: cin, cout
  BitSelector #(.group(7), .width(32)) bitselector_9 (.in(inst), .out(opcode), .sel(3'b000));
  Multiplexer #(.enable("false"), .width(32)) multiplexer_1 (
    .in0(multiplexer_2_out), .in1(imm_I), .out(imm), .sel(comparator_1_eq));
  Comparator #(.mode("unsigned"), .width(7)) comparator_1 (
    .a(opcode), .b(7'b1110011), .eq(comparator_1_eq));  // open: gt, lt
  Adder #(.width(32)) adder_6 (.a(adder_4_out), .b(adder_5_out), .out(imm_S));  // open: cin, cout
  Multiplexer #(.enable("false"), .select(3), .width(32)) multiplexer_2 (
    .in1(imm_I), .in2(imm_S), .in3(imm_SB), .in4(imm_U), .in5(imm_UJ), .out(multiplexer_2_out), .sel(ImmSel));  // open: in0, in6, in7
  assign bit_extender_10_out = {{31{i_31}}, i_31};  // Bit_Extender bit_extender_10
  assign bit_extender_11_out = {{31{1'b0}}, i_7};  // Bit_Extender bit_extender_11
  assign bit_extender_12_out = {{31{1'b0}}, i_31};  // Bit_Extender bit_extender_12
  assign bit_extender_13_out = {{31{i_31}}, i_31};  // Bit_Extender bit_extender_13
  assign bit_extender_14_out = {{31{1'b0}}, i_20};  // Bit_Extender bit_extender_14
  Shifter #(.width(32)) shifter_13 (.in(bit_extender_10_out), .\dist (5'b01100), .out(shifter_13_out));
  Shifter #(.width(32)) shifter_14 (.in(bit_extender_11_out), .\dist (5'b01011), .out(shifter_14_out));
  Shifter #(.width(32)) shifter_15 (.in(bit_extender_12_out), .\dist ({5{1'b1}}), .out(shifter_15_out));
  Shifter #(.width(32)) shifter_16 (.in(bit_extender_13_out), .\dist (5'b10100), .out(shifter_16_out));
  Shifter #(.width(32)) shifter_17 (.in(bit_extender_14_out), .\dist (5'b01011), .out(shifter_17_out));
  Adder #(.width(32)) adder_7 (.a(shifter_13_out), .b(i_30_25), .out(adder_7_out));  // open: cin, cout
  Adder #(.width(32)) adder_8 (.a(i_11_8), .b(shifter_14_out), .out(adder_8_out));  // open: cin, cout
  Adder #(.width(32)) adder_9 (.a(shifter_15_out), .b(i_30_20), .out(adder_9_out));  // open: cin, cout
  Adder #(.width(32)) adder_10 (.a(shifter_16_out), .b(i_19_12), .out(adder_10_out));  // open: cin, cout
  Adder #(.width(32)) adder_11 (.a(i_30_25), .b(shifter_17_out), .out(adder_11_out));  // open: cin, cout
  Adder #(.width(32)) adder_12 (.a(adder_7_out), .b(adder_8_out), .out(imm_SB));  // open: cin, cout
  Adder #(.width(32)) adder_13 (.a(adder_9_out), .b(i_19_12), .out(imm_U));  // open: cin, cout
  Adder #(.width(32)) adder_14 (.a(adder_10_out), .b(adder_11_out), .out(adder_14_out));  // open: cin, cout
  Adder #(.width(32)) adder_15 (.a(adder_14_out), .b(i_24_21), .out(imm_UJ));  // open: cin, cout

  // Notes on the sheet:
  //   INPUTS to your circuit
  //   inst[30:25]
  //   inst[24:21]
  //   inst[11:8]
  //   inst[19:12]
  //   inst[30:20]
  //   DON'T CHANGE THE LOCATIONS OF THE INPUTS AND OUTPUTS!
  //   OUTPUT from your circuit
endmodule
