// Logisim project regfile.circ as structural Verilog: 1 circuit, main circuit regfile
module regfile (
  input  [4:0] rs1,
  input  [4:0] rs2,
  input  [4:0] rd,
  input  [31:0] Write_Data,
  input  RegWEn,
  input  clk,
  output [31:0] ra,
  output [31:0] sp,
  output [31:0] t0,
  output [31:0] t1,
  output [31:0] t2,
  output [31:0] s0,
  output [31:0] s1,
  output [31:0] a0,
  output [31:0] Read_Data_1,
  output [31:0] Read_Data_2
);

  wire and_1_out, and_2_out, and_3_out, and_4_out, and_5_out, and_6_out, and_7_out, and_8_out, and_9_out,
       and_10_out, and_11_out, and_12_out, and_13_out, and_14_out, and_15_out, and_16_out, and_17_out,
       and_18_out, and_19_out, and_20_out, and_21_out, and_22_out, and_23_out, and_24_out, and_25_out,
       and_26_out, and_27_out, and_28_out, and_29_out, and_30_out, and_31_out, comparator_1_eq,
       comparator_2_eq, comparator_3_eq, comparator_4_eq, comparator_5_eq, comparator_6_eq, comparator_7_eq,
       comparator_8_eq, comparator_9_eq, comparator_10_eq, comparator_11_eq, comparator_12_eq,
       comparator_13_eq, comparator_14_eq, comparator_15_eq, comparator_16_eq, comparator_17_eq,
       comparator_18_eq, comparator_19_eq, comparator_20_eq, comparator_21_eq, comparator_22_eq,
       comparator_23_eq, comparator_24_eq, comparator_25_eq, comparator_26_eq, comparator_27_eq,
       comparator_28_eq, comparator_29_eq, comparator_30_eq, comparator_31_eq;
  wire [31:0] x3_out, x4_out, x11_out, x12_out, x13_out, x14_out, x15_out, x16_out, x17_out, x18_out,
       x19_out, x20_out, x21_out, x22_out, x23_out, x24_out, x25_out, x26_out, x27_out, x28_out, x29_out,
       x30_out, x31_out;

  Comparator #(.width(5)) comparator_1 (.a(rd), .b(5'b00001), .eq(comparator_1_eq));  // open: gt, lt
  Comparator #(.width(5)) comparator_2 (.a(rd), .b(5'b00010), .eq(comparator_2_eq));  // open: gt, lt
  Comparator #(.width(5)) comparator_3 (.a(rd), .b(5'b00011), .eq(comparator_3_eq));  // open: gt, lt
  Comparator #(.width(5)) comparator_4 (.a(rd), .b(5'b00100), .eq(comparator_4_eq));  // open: gt, lt
  Comparator #(.width(5)) comparator_5 (.a(rd), .b(5'b00101), .eq(comparator_5_eq));  // open: gt, lt
  Comparator #(.width(5)) comparator_6 (.a(rd), .b(5'b00110), .eq(comparator_6_eq));  // open: gt, lt
  Comparator #(.width(5)) comparator_7 (.a(rd), .b(5'b00111), .eq(comparator_7_eq));  // open: gt, lt
  and and_1 (and_1_out, RegWEn, comparator_1_eq);
  and and_2 (and_2_out, RegWEn, comparator_2_eq);
  and and_3 (and_3_out, RegWEn, comparator_3_eq);
  and and_4 (and_4_out, RegWEn, comparator_4_eq);
  and and_5 (and_5_out, RegWEn, comparator_5_eq);
  and and_6 (and_6_out, RegWEn, comparator_6_eq);
  and and_7 (and_7_out, RegWEn, comparator_7_eq);
  Register #(.width(32)) x1 (.D(Write_Data), .en(and_1_out), .clk(clk), .Q(ra));  // open: clr
  Register #(.width(32)) x2 (.D(Write_Data), .en(and_2_out), .clk(clk), .Q(sp));  // open: clr
  Register #(.width(32)) x3 (.D(Write_Data), .en(and_3_out), .clk(clk), .Q(x3_out));  // open: clr
  Register #(.width(32)) x4 (.D(Write_Data), .en(and_4_out), .clk(clk), .Q(x4_out));  // open: clr
  Register #(.width(32)) x5 (.D(Write_Data), .en(and_5_out), .clk(clk), .Q(t0));  // open: clr
  Register #(.width(32)) x6 (.D(Write_Data), .en(and_6_out), .clk(clk), .Q(t1));  // open: clr
  Register #(.width(32)) x7 (.D(Write_Data), .en(and_7_out), .clk(clk), .Q(t2));  // open: clr
  Multiplexer #(.enable("false"), .select(5), .width(32)) multiplexer_1 (
    .in0({32{1'b0}}), .in1(ra), .in2(sp), .in3(x3_out), .in4(x4_out), .in5(t0), .in6(t1), .in7(t2), .in8(s0),
    .in9(s1), .in10(a0), .in11(x11_out), .in12(x12_out), .in13(x13_out), .in14(x14_out), .in15(x15_out),
    .in16(x16_out), .in17(x17_out), .in18(x18_out), .in19(x19_out), .in20(x20_out), .in21(x21_out),
    .in22(x22_out), .in23(x23_out), .in24(x24_out), .in25(x25_out), .in26(x26_out), .in27(x27_out),
    .in28(x28_out), .in29(x29_out), .in30(x30_out), .in31(x31_out), .out(Read_Data_1), .sel(rs1));
  Comparator #(.width(5)) comparator_8 (.a(rd), .b(5'b01000), .eq(comparator_8_eq));  // open: gt, lt
  Comparator #(.width(5)) comparator_9 (.a(rd), .b(5'b01001), .eq(comparator_9_eq));  // open: gt, lt
  Comparator #(.width(5)) comparator_10 (.a(rd), .b(5'b01010), .eq(comparator_10_eq));  // open: gt, lt
  Comparator #(.width(5)) comparator_11 (.a(rd), .b(5'b01011), .eq(comparator_11_eq));  // open: gt, lt
  Comparator #(.width(5)) comparator_12 (.a(rd), .b(5'b01100), .eq(comparator_12_eq));  // open: gt, lt
  Comparator #(.width(5)) comparator_13 (.a(rd), .b(5'b01101), .eq(comparator_13_eq));  // open: gt, lt
  Comparator #(.width(5)) comparator_14 (.a(rd), .b(5'b01110), .eq(comparator_14_eq));  // open: gt, lt
  Comparator #(.width(5)) comparator_15 (.a(rd), .b(5'b01111), .eq(comparator_15_eq));  // open: gt, lt
  Register #(.width(32)) register_1 (.D(Write_Data), .en(and_8_out), .clk(clk), .Q(s0));  // open: clr
  and and_8 (and_8_out, RegWEn, comparator_8_eq);
  Register #(.width(32)) register_2 (.D(Write_Data), .en(and_9_out), .clk(clk), .Q(s1));  // open: clr
  and and_9 (and_9_out, RegWEn, comparator_9_eq);
  Register #(.width(32)) register_3 (.D(Write_Data), .en(and_10_out), .clk(clk), .Q(a0));  // open: clr
  and and_10 (and_10_out, RegWEn, comparator_10_eq);
  Register #(.width(32)) register_4 (.D(Write_Data), .en(and_11_out), .clk(clk), .Q(x11_out));  // open: clr
  and and_11 (and_11_out, RegWEn, comparator_11_eq);
  Register #(.width(32)) register_5 (.D(Write_Data), .en(and_12_out), .clk(clk), .Q(x12_out));  // open: clr
  and and_12 (and_12_out, RegWEn, comparator_12_eq);
  Register #(.width(32)) register_6 (.D(Write_Data), .en(and_13_out), .clk(clk), .Q(x13_out));  // open: clr
  and and_13 (and_13_out, RegWEn, comparator_13_eq);
  Register #(.width(32)) register_7 (.D(Write_Data), .en(and_14_out), .clk(clk), .Q(x14_out));  // open: clr
  and and_14 (and_14_out, RegWEn, comparator_14_eq);
  Register #(.width(32)) register_8 (.D(Write_Data), .en(and_15_out), .clk(clk), .Q(x15_out));  // open: clr
  and and_15 (and_15_out, RegWEn, comparator_15_eq);
  Multiplexer #(.enable("false"), .select(5), .width(32)) multiplexer_2 (
    .in0({32{1'b0}}), .in1(ra), .in2(sp), .in3(x3_out), .in4(x4_out), .in5(t0), .in6(t1), .in7(t2), .in8(s0),
    .in9(s1), .in10(a0), .in11(x11_out), .in12(x12_out), .in13(x13_out), .in14(x14_out), .in15(x15_out),
    .in16(x16_out), .in17(x17_out), .in18(x18_out), .in19(x19_out), .in20(x20_out), .in21(x21_out),
    .in22(x22_out), .in23(x23_out), .in24(x24_out), .in25(x25_out), .in26(x26_out), .in27(x27_out),
    .in28(x28_out), .in29(x29_out), .in30(x30_out), .in31(x31_out), .out(Read_Data_2), .sel(rs2));
  Comparator #(.width(5)) comparator_16 (.a(rd), .b(5'b10000), .eq(comparator_16_eq));  // open: gt, lt
  Comparator #(.width(5)) comparator_17 (.a(rd), .b(5'b10001), .eq(comparator_17_eq));  // open: gt, lt
  Comparator #(.width(5)) comparator_18 (.a(rd), .b(5'b10010), .eq(comparator_18_eq));  // open: gt, lt
  Comparator #(.width(5)) comparator_19 (.a(rd), .b(5'b10011), .eq(comparator_19_eq));  // open: gt, lt
  Comparator #(.width(5)) comparator_20 (.a(rd), .b(5'b10100), .eq(comparator_20_eq));  // open: gt, lt
  Comparator #(.width(5)) comparator_21 (.a(rd), .b(5'b10101), .eq(comparator_21_eq));  // open: gt, lt
  Comparator #(.width(5)) comparator_22 (.a(rd), .b(5'b10110), .eq(comparator_22_eq));  // open: gt, lt
  Comparator #(.width(5)) comparator_23 (.a(rd), .b(5'b10111), .eq(comparator_23_eq));  // open: gt, lt
  Register #(.width(32)) register_9 (.D(Write_Data), .en(and_16_out), .clk(clk), .Q(x16_out));  // open: clr
  and and_16 (and_16_out, RegWEn, comparator_16_eq);
  Register #(.width(32)) register_10 (.D(Write_Data), .en(and_17_out), .clk(clk), .Q(x17_out));  // open: clr
  and and_17 (and_17_out, RegWEn, comparator_17_eq);
  Register #(.width(32)) register_11 (.D(Write_Data), .en(and_18_out), .clk(clk), .Q(x18_out));  // open: clr
  and and_18 (and_18_out, RegWEn, comparator_18_eq);
  Register #(.width(32)) register_12 (.D(Write_Data), .en(and_19_out), .clk(clk), .Q(x19_out));  // open: clr
  and and_19 (and_19_out, RegWEn, comparator_19_eq);
  Register #(.width(32)) register_13 (.D(Write_Data), .en(and_20_out), .clk(clk), .Q(x20_out));  // open: clr
  and and_20 (and_20_out, RegWEn, comparator_20_eq);
  Register #(.width(32)) register_14 (.D(Write_Data), .en(and_21_out), .clk(clk), .Q(x21_out));  // open: clr
  and and_21 (and_21_out, RegWEn, comparator_21_eq);
  Register #(.width(32)) register_15 (.D(Write_Data), .en(and_22_out), .clk(clk), .Q(x22_out));  // open: clr
  and and_22 (and_22_out, RegWEn, comparator_22_eq);
  Register #(.width(32)) register_16 (.D(Write_Data), .en(and_23_out), .clk(clk), .Q(x23_out));  // open: clr
  and and_23 (and_23_out, RegWEn, comparator_23_eq);
  Comparator #(.width(5)) comparator_24 (.a(rd), .b(5'b11000), .eq(comparator_24_eq));  // open: gt, lt
  Comparator #(.width(5)) comparator_25 (.a(rd), .b(5'b11001), .eq(comparator_25_eq));  // open: gt, lt
  Comparator #(.width(5)) comparator_26 (.a(rd), .b(5'b11010), .eq(comparator_26_eq));  // open: gt, lt
  Comparator #(.width(5)) comparator_27 (.a(rd), .b(5'b11011), .eq(comparator_27_eq));  // open: gt, lt
  Comparator #(.width(5)) comparator_28 (.a(rd), .b(5'b11100), .eq(comparator_28_eq));  // open: gt, lt
  Comparator #(.width(5)) comparator_29 (.a(rd), .b(5'b11101), .eq(comparator_29_eq));  // open: gt, lt
  Comparator #(.width(5)) comparator_30 (.a(rd), .b(5'b11110), .eq(comparator_30_eq));  // open: gt, lt
  Comparator #(.width(5)) comparator_31 (.a(rd), .b({5{1'b1}}), .eq(comparator_31_eq));  // open: gt, lt
  Register #(.width(32)) register_17 (.D(Write_Data), .en(and_24_out), .clk(clk), .Q(x24_out));  // open: clr
  and and_24 (and_24_out, RegWEn, comparator_24_eq);
  Register #(.width(32)) register_18 (.D(Write_Data), .en(and_25_out), .clk(clk), .Q(x25_out));  // open: clr
  and and_25 (and_25_out, RegWEn, comparator_25_eq);
  Register #(.width(32)) register_19 (.D(Write_Data), .en(and_26_out), .clk(clk), .Q(x26_out));  // open: clr
  and and_26 (and_26_out, RegWEn, comparator_26_eq);
  Register #(.width(32)) register_20 (.D(Write_Data), .en(and_27_out), .clk(clk), .Q(x27_out));  // open: clr
  and and_27 (and_27_out, RegWEn, comparator_27_eq);
  Register #(.width(32)) register_21 (.D(Write_Data), .en(and_28_out), .clk(clk), .Q(x28_out));  // open: clr
  and and_28 (and_28_out, RegWEn, comparator_28_eq);
  Register #(.width(32)) register_22 (.D(Write_Data), .en(and_29_out), .clk(clk), .Q(x29_out));  // open: clr
  and and_29 (and_29_out, RegWEn, comparator_29_eq);
  Register #(.width(32)) register_23 (.D(Write_Data), .en(and_30_out), .clk(clk), .Q(x30_out));  // open: clr
  and and_30 (and_30_out, RegWEn, comparator_30_eq);
  Register #(.width(32)) register_24 (.D(Write_Data), .en(and_31_out), .clk(clk), .Q(x31_out));  // open: clr
  and and_31 (and_31_out, RegWEn, comparator_31_eq);

  // Other names for the same wires on the sheet: read_data1[31:0] = Read_Data_1; read_data2[31:0] = Read_Data_2;
  //   read_reg1[4:0] = rs1; read_reg2[4:0] = rs2; write_en = RegWEn; write_reg[4:0] = rd; x1_out[31:0] = ra;
  //   x2_out[31:0] = sp; x5_out[31:0] = t0; x6_out[31:0] = t1; x7_out[31:0] = t2; x8_out[31:0] = s0;
  //   x9_out[31:0] = s1; x10_out[31:0] = a0

  // Notes on the sheet:
  //   INPUTS to your circuit
  //   DON'T CHANGE THE LOCATIONS OF THE INPUTS AND OUTPUTS!
  //   These are DEBUG/TEST outputs from your circuit.
  //   OUTPUTS from your circuit
endmodule
